# Fritzing sketch Prototype (saved by Fritzing 0.9.2b)
circuit board: 3.67895cm x 8.67416cm
breadboards: 1

parts:
  Front_Sensor = HC-SR04
  Left_Sensor = HC-SR04
  Right_sensor = HC-SR04
  Teensy_2_0 = Teensy 2.0
  ESP8266 = ESP8266 WiFi Module [part_number=ESP8266]
  Regulator_3_3v = Voltage Regulator - 3.3V [package="TO220 [THT]"]

nets:
  VCC: Front_Sensor.VCC, Left_Sensor.VCC, Right_sensor.VCC, Teensy_2_0.VCC, Regulator_3_3v.input_voltage
  N1: Front_Sensor.Trig, Teensy_2_0.F0
  N2: Front_Sensor.Echo, Teensy_2_0.F1
  GND: Front_Sensor.GND, Left_Sensor.GND, Right_sensor.GND, Teensy_2_0.GND, ESP8266.GND, Regulator_3_3v.GND
  N3: Left_Sensor.Trig, Teensy_2_0.F4
  N4: Left_Sensor.Echo, Teensy_2_0.F5
  N5: Right_sensor.Trig, Teensy_2_0.F6
  N6: Right_sensor.Echo, Teensy_2_0.F7
  N7: Teensy_2_0.D2, ESP8266.TXD
  N8: Teensy_2_0.D3, ESP8266.RXD
  N9: ESP8266.VCC, ESP8266.CH_PD, Regulator_3_3v.output_voltage

custom parts:
  HC-SR04: Ultrasonic ranging module HC - SR04 provides 2cm - 400cm non-contact measurement function, the ranging accuracy can reach to 3mm. The modules includes ultrasonic transmitters, receiver and control circuit
  ESP8266 WiFi Module: Generic WiFi Module based on the ESP8266 with onboard PCB antenna and UART communications
  Voltage Regulator - 3.3V: 3.3V DC Voltage Regulator
